// Logisim project 2a given.circ as structural Verilog: 1 circuit, main circuit main
module main (
  input  A,
  input  B,
  input  C,
  input  D,
  output Y
);

  wire AND_2_out, AND_3_out, AND_out, NOT_2_out, NOT_3_out, NOT_4_out, NOT_out;

  not NOT (NOT_out, A);
  not NOT_2 (NOT_2_out, B);
  not NOT_3 (NOT_3_out, C);
  not NOT_4 (NOT_4_out, D);
  and AND (AND_out, NOT_out, B, NOT_4_out);
  and AND_2 (AND_2_out, A, NOT_2_out, NOT_3_out, NOT_4_out);
  and AND_3 (AND_3_out, NOT_out, NOT_2_out, NOT_3_out, D);
  or OR (Y, AND_out, AND_2_out, AND_3_out);
endmodule
