// Logisim project 2a.circ as structural Verilog: 1 circuit, main circuit main
module main (
  input  X1,
  input  X2,
  input  X3,
  input  X4,
  output A_X1_X2_X3_X4
);

  wire AND_out, OR_out;

  and AND (AND_out, X3, X4);
  or OR (OR_out, X2, AND_out);
  and AND_2 (A_X1_X2_X3_X4, X1, OR_out);
endmodule
