// Logisim project 2b code converter 2).circ as structural Verilog: 1 circuit, main circuit main
module main (
  input  E3,
  input  E2,
  input  E1,
  input  E0,
  output B3,
  output B2,
  output B1,
  output B0
);

  wire AND_2_out, AND_3_out, AND_4_out, AND_5_out, AND_6_out, AND_7_out, AND_out, NOT_2_out, NOT_3_out,
       NOT_4_out, NOT_5_out, NOT_6_out, NOT_7_out;

  or OR (B2, AND_out, AND_2_out, AND_3_out);
  or OR_2 (B1, AND_4_out, AND_5_out);
  or OR_3 (B3, AND_6_out, AND_7_out);
  and AND (AND_out, NOT_2_out, NOT_3_out);
  and AND_2 (AND_2_out, NOT_4_out, NOT_5_out);
  and AND_3 (AND_3_out, E2, E1, E0);
  and AND_4 (AND_4_out, NOT_6_out, E0);
  and AND_5 (AND_5_out, E1, NOT_7_out);
  not NOT (B0, E0);
  and AND_6 (AND_6_out, E3, E1, E0);
  and AND_7 (AND_7_out, E3, E2);
  not NOT_2 (NOT_2_out, E2);
  not NOT_3 (NOT_3_out, E1);
  not NOT_4 (NOT_4_out, E2);
  not NOT_5 (NOT_5_out, E0);
  not NOT_6 (NOT_6_out, E1);
  not NOT_7 (NOT_7_out, E0);
endmodule
