// Logisim project 2b.circ as structural Verilog: 1 circuit, main circuit main
module main (
  input  D,
  input  C,
  input  B,
  input  A,
  output Z,
  output Y,
  output X,
  output W
);

  wire and_1_out, and_2_out, and_3_out, and_4_out, not_2_out, not_3_out, or_1_out;

  not not_1 (Z, C);
  and and_1 (and_1_out, C, C);
  or or_1 (or_1_out, C, C);
  not not_2 (not_2_out, B);
  not not_3 (not_3_out, or_1_out);
  and and_2 (and_2_out, or_1_out, not_2_out);
  and and_3 (and_3_out, or_1_out, B);
  or or_2 (Y, and_1_out, not_3_out);
  and and_4 (and_4_out, not_3_out, B);
  or or_3 (W, and_3_out, A);
  or or_4 (X, and_4_out, and_2_out);

  assign D = C;
endmodule
