// Logisim project 3 FULL ADDER.circ as structural Verilog: 1 circuit, main circuit main
module main (
  input  A,
  input  B,
  input  C,
  output SUM,
  output CARRY
);

  wire AND_2_out, AND_out, XNOR_out;

  xor XNOR (XNOR_out, A, B);
  and AND (AND_out, A, B);
  and AND_2 (AND_2_out, XNOR_out, C);
  xor XNOR_2 (SUM, XNOR_out, C);
  or OR (CARRY, AND_2_out, AND_out);
endmodule
