// Logisim project 3 HALF ADDER.circ as structural Verilog: 1 circuit, main circuit main
module main (
  input  A,
  input  B,
  output SUM,
  output CARRY
);

  xor XOR (SUM, A, B);
  and AND (CARRY, A, B);

  // Notes on the sheet:
  //   Half adder
endmodule
