// Logisim project 3 HALF SUBTRACTOR.circ as structural Verilog: 1 circuit, main circuit main
module main (
  input  A,
  input  B,
  output DIFFERENCE,
  output BORROW
);

  wire not_1_out;

  not not_1 (not_1_out, A);
  xor XOR (DIFFERENCE, A, B);
  and AND (BORROW, not_1_out, B);

  // Notes on the sheet:
  //   HALF SUBTRACTOR
endmodule
