// Logisim project 4C.circ as structural Verilog: 1 circuit, main circuit main
module main (
  input  Y0,
  input  Y1,
  input  Y2,
  output A1,
  output A1_2
);

  or or_1 (A1, Y0, Y1);
  or or_2 (A1_2, Y0, Y2);

  // Notes on the sheet:
  //   EXCERISE NO 4C
endmodule
