// Logisim project 4D.circ as structural Verilog: 1 circuit, main circuit main
module main (
  input  A0,
  input  A1,
  input  E,
  output Y3,
  output Y2,
  output Y1,
  output Y0
);

  wire not_1_out, not_2_out;

  not not_1 (not_1_out, A0);
  not not_2 (not_2_out, A1);
  and and_1 (Y3, A0, A1, E);
  and and_2 (Y2, A0, not_2_out, E);
  and and_3 (Y1, not_1_out, A1, E);
  and and_4 (Y0, not_1_out, not_2_out, E);
endmodule
