// Logisim project 4a add sub.circ as structural Verilog: 1 circuit, main circuit main
module main (
  input  B3,
  input  A3,
  input  B2,
  input  A2,
  input  B1,
  input  A1,
  input  B0,
  input  A0,
  input  K,
  output S0,
  output C,
  output S3,
  output S2,
  output S1
);

  wire adder_2_cout, adder_3_cout, adder_4_cout, xor_1_out, xor_2_out, xor_3_out, xor_4_out;

  xor xor_1 (xor_1_out, B3, K);
  xor xor_2 (xor_2_out, B2, K);
  Adder #(.width(1)) adder_1 (.a(A3), .b(xor_1_out), .out(S3), .cin(adder_2_cout), .cout(C));
  Adder #(.width(1)) adder_2 (.a(A2), .b(xor_2_out), .out(S2), .cin(adder_3_cout), .cout(adder_2_cout));
  xor xor_3 (xor_3_out, B1, K);
  Adder #(.width(1)) adder_3 (.a(A1), .b(xor_3_out), .out(S1), .cin(adder_4_cout), .cout(adder_3_cout));
  xor xor_4 (xor_4_out, B0, K);
  Adder #(.width(1)) adder_4 (.a(A0), .b(xor_4_out), .out(S0), .cin(K), .cout(adder_4_cout));
endmodule
