// Logisim project 4a_add_4b_sub.circ as structural Verilog: 1 circuit, main circuit main
module main (
  input  b3,
  input  a3,
  input  b2,
  input  a2,
  input  b1,
  input  a1,
  input  b0,
  input  a0,
  input  k,
  input  in_10,
  input  [3:0] in_11,
  input  [3:0] in_12,
  input  [3:0] in_13,
  input  [3:0] in_14,
  input  in_15,
  output c_out,
  output s3,
  output s2,
  output s0,
  output s1,
  output out_21,
  output out_22,
  output out_23
);

  wire adder_3_cout, adder_5_cout, adder_6_cout, and_1_out, and_2_out, xor_1_out, xor_2_out, xor_3_out,
       xor_4_out;
  wire [2:2] or_1_out;

  xor xor_1 (xor_1_out, b3, k);
  or or_1 (or_1_out[2], out_21, and_1_out, and_2_out);
  and and_1 (and_1_out, in_12[2], in_12[3]);
  and and_2 (and_2_out, in_12[1], in_12[3]);
  Adder #(.width(1)) adder_1 (.a(a3), .b(xor_1_out), .out(s3), .cin(adder_3_cout), .cout(c_out));
  xor xor_2 (xor_2_out, b2, k);
  Adder #(.width(4)) adder_2 (.a(in_11), .b(in_13), .out(in_12), .cin(in_10), .cout(out_21));
  Adder #(.width(1)) adder_3 (.a(a2), .b(xor_2_out), .out(s2), .cin(adder_5_cout), .cout(adder_3_cout));
  Adder #(.width(4)) adder_4 (
    .a(in_12), .b({in_15, {2{or_1_out[2]}}, in_15}), .out(in_14), .cin(out_21), .cout(out_22));
  xor xor_3 (xor_3_out, b1, k);
  Adder #(.width(1)) adder_5 (.a(a1), .b(xor_3_out), .out(s1), .cin(adder_6_cout), .cout(adder_5_cout));
  xor xor_4 (xor_4_out, b0, k);
  Adder #(.width(1)) adder_6 (.a(a0), .b(xor_4_out), .out(s0), .cin(k), .cout(adder_6_cout));
endmodule
