// Logisim project A(A+B)=A.circ as structural Verilog: 1 circuit, main circuit main
module main (
  input  A,
  input  B,
  output C
);

  wire OR_out;

  or OR (OR_out, A, B);
  and AND (C, A, OR_out);
endmodule
