// Logisim project A(B+C).circ as structural Verilog: 1 circuit, main circuit main
module main (
  input  A,
  input  B,
  input  C,
  output D
);

  wire OR_out;

  or OR (OR_out, B, C);
  and AND (D, A, OR_out);
endmodule
