// Logisim project A+AB=A.circ as structural Verilog: 1 circuit, main circuit main
module main (
  input  A,
  input  B,
  output C
);

  wire AND_out;

  and AND (AND_out, A, B);
  or OR (C, A, AND_out);
endmodule
