// Logisim project A+B=B+A.circ as structural Verilog: 1 circuit, main circuit main
module main (
  input  A,
  input  B,
  output x
);

  or or_1 (x, A, B);

  // Notes on the sheet:
  //   A+B
endmodule
