// Logisim project A+~AB=A+B.circ as structural Verilog: 1 circuit, main circuit main
module main (
  input  A,
  input  B,
  output C
);

  wire AND_out, NOT_out;

  not NOT (NOT_out, A);
  and AND (AND_out, NOT_out, B);
  or OR (C, A, AND_out);
endmodule
