// Logisim project AB+AC.circ as structural Verilog: 1 circuit, main circuit main
module main (
  input  A,
  input  B,
  input  C,
  output D
);

  wire AND_2_out, AND_out;

  and AND (AND_out, A, B);
  and AND_2 (AND_2_out, A, C);
  or OR (D, AND_out, AND_2_out);
endmodule
