// Logisim project COMMUA+B=B+A.circ as structural Verilog: 1 circuit, main circuit main
module main (
  input  A,
  input  B,
  input  A_2,
  input  B_2,
  output C,
  output C_2
);

  or OR (C, A, B_2);
  or OR_2 (C_2, B, A_2);
endmodule
