// Logisim project EX 2b.circ as structural Verilog: 1 circuit, main circuit main
module main (
  input  C,
  input  D,
  input  B,
  input  A,
  output Z,
  output Y,
  output X,
  output W
);

  wire and_1_out, and_2_out, and_3_out, and_4_out, not_2_out, not_3_out, or_1_out;

  not not_1 (Z, C);
  not not_2 (not_2_out, B);
  and and_1 (and_1_out, C, D);
  or or_1 (or_1_out, C, D);
  not not_3 (not_3_out, or_1_out);
  or or_2 (Y, and_1_out, not_3_out);
  and and_2 (and_2_out, not_3_out, B);
  and and_3 (and_3_out, or_1_out, not_2_out);
  and and_4 (and_4_out, or_1_out, B);
  or or_3 (X, and_2_out, and_3_out);
  or or_4 (W, and_4_out, A);

  // Notes on the sheet:
  //   D'
  //   CD
  //   C+D
  //   (C+D)'
endmodule
