// Logisim project FULL ADDER USING MUX.circ as structural Verilog: 1 circuit, main circuit main
module main (
  input  in_1,
  input  [1:0] in_2,
  output SUM,
  output CARRY
);

  wire not_1_out;

  not not_1 (not_1_out, in_1);
  Multiplexer #(.select(2)) multiplexer_1 (
    .in0(in_1), .in1(not_1_out), .in2(not_1_out), .in3(in_1), .out(SUM), .sel(in_2));  // open: en
  Multiplexer #(.select(2)) multiplexer_2 (
    .in0(1'b0), .in1(in_1), .in2(in_1), .in3(1'b1), .out(CARRY), .sel(in_2));  // open: en

  // Notes on the sheet:
  //   FULL ADDER USING MUX
endmodule
