// Logisim project FULL SUBRACTOR EXAMPLE.circ as structural Verilog: 1 circuit, main circuit main
module main (
  input  A,
  input  B,
  input  C,
  output D
);

  wire AND_2_out, AND_out, NOR_out, NOT_2_out, NOT_out;

  not NOT (NOT_out, A);
  xor NOR (NOR_out, A, B);
  not NOT_2 (NOT_2_out, NOR_out);
  and AND (AND_out, NOT_out, B);
  and AND_2 (AND_2_out, NOT_2_out, C);
  or OR (D, AND_2_out, AND_out);
endmodule
