// Logisim project GATES.circ as structural Verilog: 1 circuit, main circuit main
module main (
  input  X,
  input  Y,
  input  A,
  input  X_2,
  input  X_3,
  input  Y_2,
  input  Y_3,
  input  X_4,
  input  X_5,
  input  Y_4,
  input  Y_5,
  input  X_6,
  input  Y_6,
  output C,
  output C_2,
  output C_3,
  output C_4,
  output C_5,
  output C_6,
  output C_7
);

  and AND (C, X, Y);
  xor XNOR (C_5, X_4, Y_4);
  nand NAND (C_7, X_6, Y_6);
  xor XOR (C_3, X_2, Y_3);
  not NOT (C_2, A);
  nor NOR (C_4, X_3, Y_2, Y_2);
  xnor XNOR_2 (C_6, X_5, Y_5);

  // Notes on the sheet:
  //   AND gate
  //   XNOR gate
  //   XNOR gate
  //   NAND gate
  //   NOT gate
  //   NOR gate
  //   XNOR gate
endmodule
