// Logisim project HALF ADDER USING MUX.circ as structural Verilog: 1 circuit, main circuit main
module main (
  input  A,
  input  B,
  output SUM,
  output CARRY
);

  wire not_1_out;

  not not_1 (not_1_out, A);
  Multiplexer multiplexer_1 (.in0(A), .in1(not_1_out), .out(SUM), .sel(B), .en(1'b1));
  Multiplexer multiplexer_2 (.in0(1'b0), .in1(A), .out(CARRY), .sel(B), .en(1'b1));

  // Notes on the sheet:
  //   HALF ADDER USING MUX
endmodule
