// Logisim project Half_adder_using_MUX.circ as structural Verilog: 1 circuit, main circuit main
module main (
  input  in_1,
  input  in_2,
  output out_3,
  output out_4
);

  wire not_1_out;

  not not_1 (not_1_out, in_1);
  Multiplexer multiplexer_1 (.in0(in_1), .in1(not_1_out), .out(out_3), .sel(in_2), .en(1'b1));
  Multiplexer multiplexer_2 (.in0(1'b0), .in1(in_1), .out(out_4), .sel(in_2), .en(1'b1));
endmodule
