// Logisim project LAW 2.circ as structural Verilog: 1 circuit, main circuit main
module main (
  input  B,
  input  C,
  input  A,
  input  B_2,
  input  C_2,
  input  A_2,
  output out_7,
  output A_B___A_C
);

  wire and_1_out, or_1_out;

  and and_1 (and_1_out, B_2, C_2);
  or or_1 (or_1_out, B, C);
  and and_2 (out_7, or_1_out, A);
  or or_2 (A_B___A_C, and_1_out, A_2);

  // Notes on the sheet:
  //   DISTRIBUTIVE LAW
  //   A.(B+C)
  //   B+C
  //   A+(B.C)
  //   A.B+A.C
endmodule
