// Logisim project LAWS.circ as structural Verilog: 1 circuit, main circuit main
module main (
  input  A,
  input  B,
  input  A_2,
  input  B_2,
  input  in_5,
  input  in_6,
  input  in_7,
  input  in_8,
  input  in_9,
  input  in_10,
  output B_A,
  output B_A_2,
  output out_13,
  output out_14
);

  wire and_2_out, or_2_out;

  or or_1 (B_A, A, B);
  and and_1 (B_A_2, A_2, B_2);
  or or_2 (or_2_out, in_5, in_6);
  and and_2 (and_2_out, in_8, in_9);
  or or_3 (out_13, or_2_out, in_7);
  and and_3 (out_14, and_2_out, in_10);

  // Notes on the sheet:
  //   COMMUTATIVE LAW
  //   1
  //   2
  //   3
  //   4
endmodule
