// Logisim project SHIFT REGISTER.circ as structural Verilog: 1 circuit, main circuit main
module main (
  input  _14,
  input  in_2,
  input  _13,
  input  _12,
  input  in_5,
  input  _11,
  input  [1:0] in_7,
  output A4,
  output A3,
  output A2,
  output A1
);

  wire button_1_out, clock_1_out, multiplexer_1_out, multiplexer_2_out, multiplexer_3_out, multiplexer_4_out;

  Multiplexer #(.select(2)) multiplexer_1 (
    .in0(A4), .in1(_14), .in2(A3), .in3(in_2), .out(multiplexer_1_out), .sel(in_7));  // open: en
  Multiplexer #(.select(2)) multiplexer_2 (
    .in0(A3), .in1(A4), .in2(A2), .in3(_13), .out(multiplexer_2_out), .sel(in_7));  // open: en
  Multiplexer #(.select(2)) multiplexer_3 (
    .in0(A2), .in1(A3), .in2(A1), .in3(_12), .out(multiplexer_3_out), .sel(in_7));  // open: en
  Multiplexer #(.select(2)) multiplexer_4 (
    .in0(A1), .in1(A2), .in2(in_5), .in3(_11), .out(multiplexer_4_out), .sel(in_7));  // open: en
  Clock clock_1 (.out(clock_1_out));
  D_Flip_Flop d_ff_1 (.clk(clock_1_out), .D(multiplexer_1_out), .Q(A4), .reset(button_1_out));  // open: Qn, preset, en
  D_Flip_Flop d_ff_2 (.clk(clock_1_out), .D(multiplexer_2_out), .Q(A3), .reset(button_1_out));  // open: Qn, preset, en
  D_Flip_Flop d_ff_3 (.clk(clock_1_out), .D(multiplexer_3_out), .Q(A2), .reset(button_1_out));  // open: Qn, preset, en
  D_Flip_Flop d_ff_4 (.clk(clock_1_out), .D(multiplexer_4_out), .Q(A1), .reset(button_1_out));  // open: Qn, preset, en
  Button button_1 (.out(button_1_out));

  // Notes on the sheet:
  //   shift right
  //   shift left
  //   select bits
  //   clock
  //   clear
endmodule
