// Logisim project absorption law[law 3].circ as structural Verilog: 1 circuit, main circuit main
module main (
  input  in_1,
  input  b,
  input  a,
  input  b_2,
  output ab,
  output a_plus,
  output a_a_b__a
);

  wire or_1_out;

  or or_1 (or_1_out, a, b_2);
  and and_1 (a_a_b__a, or_1_out, a);
  and and_2 (ab, in_1, b);
  or or_2 (a_plus, ab, in_1);

  // Notes on the sheet:
  //   absorption law
  //   2
  //   1
  //   a
  //   a
  //   a+ab=a
endmodule
