// Logisim project syncronous counter.circ as structural Verilog: 1 circuit, main circuit main
module main (
  output out_1,
  output out_2,
  output OA,
  output out_4
);

  wire AND_2_out, AND_out, clock_1_out;

  Clock clock_1 (.out(clock_1_out));
  J_K_Flip_Flop j_k_ff_1 (.J(1'b1), .clk(clock_1_out), .K(1'b1), .Q(out_4));  // open: Qn, preset, en, reset
  J_K_Flip_Flop j_k_ff_2 (.J(out_4), .clk(clock_1_out), .K(out_4), .Q(out_1));  // open: Qn, preset, en, reset
  and AND (AND_out, out_4, out_1);
  J_K_Flip_Flop j_k_ff_3 (.J(AND_out), .clk(clock_1_out), .K(AND_out), .Q(out_2));  // open: Qn, preset, en, reset
  and AND_2 (AND_2_out, AND_out, out_2);
  J_K_Flip_Flop j_k_ff_4 (.J(AND_2_out), .clk(clock_1_out), .K(AND_2_out), .Q(OA));  // open: Qn, preset, en, reset

  // Notes on the sheet:
  //   clock
  //   high level
  //   OD
  //   SYNCHROUNOUS UP - COUNTER
  //   OC
  //   OB
endmodule
