// Logisim project tautology law.circ as structural Verilog: 1 circuit, main circuit main
module main (
  input  a,
  input  a_2,
  input  a_3,
  input  a_4,
  output a_a,
  output a_a_2
);

  or or_1 (a_a, a, a_2);
  and and_1 (a_a_2, a_3, a_4);

  // Notes on the sheet:
  //   TAUTOLOGY LAW
endmodule
